# Fritzing sketch scheme (saved by Fritzing 0.8.7b)

parts:
  U1 = ESP8266 NodeMCU LoLin module
  U2 = ESP8266 NodeMCU LoLin module
  S1 = Pushbutton [package="[SMD]"]
  S2 = Pushbutton [package="[SMD]"]
  R1 = Resistor [package="2010 [SMD]"]
  R2 = Resistor [package="2010 [SMD]"]

nets:
  N1: U1.3V3, S2.Pin_4
  N2: U1.GND, R2.Pin_0
  N3: U1.D5, S2.Pin_1, S2.Pin_2, R2.Pin_1
  N4: U2.3V3, R1.Pin_0
  N5: U2.GND, S1.Pin_4
  N6: U2.D5, S1.Pin_1, S1.Pin_2, R1.Pin_1

custom parts:
  ESP8266 NodeMCU LoLin module: ESP8266 based NodeMCU
